// Logisim project calculatorCPU.circ as structural Verilog: 22 circuits, main circuit main
module main (
);

  wire _0_out, _1_out, _2_out, _3_out, _4_out, _5_out, _6_out, _7_out, _8_out, _9_out, button_2_out,
       button_3_out, button_4_out, button_5_out, button_out, C_out, keypad_controller_1_write;
  wire [2:0] lcd_controller_1__7_segment_3_2, lcd_controller_1__7_segment_4_2,
       lcd_controller_1__7_segment_5_2, lcd_controller_1__7_segment_6_2, lcd_controller_1__7_segment_7_2,
       lcd_controller_1__7_segment_8_2, lcd_controller_1__7_segment_9_2, lcd_controller_1_minus_2;
  wire [3:0] lcd_controller_1__7_segment_3, lcd_controller_1__7_segment_4, lcd_controller_1__7_segment_5,
       lcd_controller_1__7_segment_6, lcd_controller_1__7_segment_7, lcd_controller_1__7_segment_8,
       lcd_controller_1__7_segment_9, lcd_controller_1_minus;
  wire [6:0] lcd_controller_1__7_segment_0, lcd_controller_1__7_segment_1, lcd_controller_1__7_segment_2;
  wire [31:0] basec_1_tokeypad, basec_1_tolcd, keypad_controller_1_output;

  baseC basec_1 (
    .Write_From_Keypad(keypad_controller_1_output), .Write_Signal(keypad_controller_1_write),
    .ToLCD(basec_1_tolcd), .ToKeypad(basec_1_tokeypad));
  _7_Segment_Display u_7_segment_display_1 (
    .g(lcd_controller_1_minus[0]), .f(lcd_controller_1_minus[1]), .a(lcd_controller_1_minus[2]),
    .b(lcd_controller_1_minus[3]), .e(lcd_controller_1_minus_2[0]), .d(lcd_controller_1_minus_2[1]),
    .c(lcd_controller_1_minus_2[2]));  // open: dp
  _7_Segment_Display u_7_segment_display_2 (
    .g(lcd_controller_1__7_segment_9[0]), .f(lcd_controller_1__7_segment_9[1]),
    .a(lcd_controller_1__7_segment_9[2]), .b(lcd_controller_1__7_segment_9[3]),
    .e(lcd_controller_1__7_segment_9_2[0]), .d(lcd_controller_1__7_segment_9_2[1]),
    .c(lcd_controller_1__7_segment_9_2[2]));  // open: dp
  LCD_Controller lcd_controller_1 (
    .From__t8(basec_1_tolcd), .Minus({lcd_controller_1_minus_2, lcd_controller_1_minus}),
    ._7_Segment_9({lcd_controller_1__7_segment_9_2, lcd_controller_1__7_segment_9}),
    ._7_Segment_8({lcd_controller_1__7_segment_8_2, lcd_controller_1__7_segment_8}),
    ._7_Segment_7({lcd_controller_1__7_segment_7_2, lcd_controller_1__7_segment_7}),
    ._7_Segment_6({lcd_controller_1__7_segment_6_2, lcd_controller_1__7_segment_6}),
    ._7_Segment_5({lcd_controller_1__7_segment_5_2, lcd_controller_1__7_segment_5}),
    ._7_Segment_4({lcd_controller_1__7_segment_4_2, lcd_controller_1__7_segment_4}),
    ._7_Segment_3({lcd_controller_1__7_segment_3_2, lcd_controller_1__7_segment_3}),
    ._7_Segment_2(lcd_controller_1__7_segment_2), ._7_Segment_1(lcd_controller_1__7_segment_1),
    ._7_Segment_0(lcd_controller_1__7_segment_0));
  Keypad_Controller keypad_controller_1 (
    .C(C_out), .in_2(button_out), .in_3(button_5_out), .in_4(button_4_out), .in_5(button_3_out),
    .in_6(button_2_out), ._9(_9_out), ._8(_8_out), ._7(_7_out), ._6(_6_out), ._5(_5_out), ._4(_4_out),
    ._3(_3_out), ._2(_2_out), ._1(_1_out), ._0(_0_out), .From__t9(basec_1_tokeypad),
    .Write(keypad_controller_1_write), .Output(keypad_controller_1_output));
  _7_Segment_Display u_7_segment_display_3 (
    .g(lcd_controller_1__7_segment_8[0]), .f(lcd_controller_1__7_segment_8[1]),
    .a(lcd_controller_1__7_segment_8[2]), .b(lcd_controller_1__7_segment_8[3]),
    .e(lcd_controller_1__7_segment_8_2[0]), .d(lcd_controller_1__7_segment_8_2[1]),
    .c(lcd_controller_1__7_segment_8_2[2]));  // open: dp
  _7_Segment_Display u_7_segment_display_4 (
    .g(lcd_controller_1__7_segment_7[0]), .f(lcd_controller_1__7_segment_7[1]),
    .a(lcd_controller_1__7_segment_7[2]), .b(lcd_controller_1__7_segment_7[3]),
    .e(lcd_controller_1__7_segment_7_2[0]), .d(lcd_controller_1__7_segment_7_2[1]),
    .c(lcd_controller_1__7_segment_7_2[2]));  // open: dp
  _7_Segment_Display u_7_segment_display_5 (
    .g(lcd_controller_1__7_segment_6[0]), .f(lcd_controller_1__7_segment_6[1]),
    .a(lcd_controller_1__7_segment_6[2]), .b(lcd_controller_1__7_segment_6[3]),
    .e(lcd_controller_1__7_segment_6_2[0]), .d(lcd_controller_1__7_segment_6_2[1]),
    .c(lcd_controller_1__7_segment_6_2[2]));  // open: dp
  _7_Segment_Display u_7_segment_display_6 (
    .g(lcd_controller_1__7_segment_5[0]), .f(lcd_controller_1__7_segment_5[1]),
    .a(lcd_controller_1__7_segment_5[2]), .b(lcd_controller_1__7_segment_5[3]),
    .e(lcd_controller_1__7_segment_5_2[0]), .d(lcd_controller_1__7_segment_5_2[1]),
    .c(lcd_controller_1__7_segment_5_2[2]));  // open: dp
  Button _7 (.out(_7_out));
  Button _4 (.out(_4_out));
  Button _1 (.out(_1_out));
  Button _0 (.out(_0_out));
  _7_Segment_Display u_7_segment_display_7 (
    .g(lcd_controller_1__7_segment_4[0]), .f(lcd_controller_1__7_segment_4[1]),
    .a(lcd_controller_1__7_segment_4[2]), .b(lcd_controller_1__7_segment_4[3]),
    .e(lcd_controller_1__7_segment_4_2[0]), .d(lcd_controller_1__7_segment_4_2[1]),
    .c(lcd_controller_1__7_segment_4_2[2]));  // open: dp
  _7_Segment_Display u_7_segment_display_8 (
    .g(lcd_controller_1__7_segment_3[0]), .f(lcd_controller_1__7_segment_3[1]),
    .a(lcd_controller_1__7_segment_3[2]), .b(lcd_controller_1__7_segment_3[3]),
    .e(lcd_controller_1__7_segment_3_2[0]), .d(lcd_controller_1__7_segment_3_2[1]),
    .c(lcd_controller_1__7_segment_3_2[2]));  // open: dp
  Button _8 (.out(_8_out));
  Button _5 (.out(_5_out));
  Button _2 (.out(_2_out));
  Button C (.out(C_out));
  _7_Segment_Display u_7_segment_display_9 (
    .g(lcd_controller_1__7_segment_2[0]), .f(lcd_controller_1__7_segment_2[1]),
    .a(lcd_controller_1__7_segment_2[2]), .b(lcd_controller_1__7_segment_2[3]),
    .e(lcd_controller_1__7_segment_2[4]), .d(lcd_controller_1__7_segment_2[5]),
    .c(lcd_controller_1__7_segment_2[6]));  // open: dp
  _7_Segment_Display u_7_segment_display_10 (
    .g(lcd_controller_1__7_segment_1[0]), .f(lcd_controller_1__7_segment_1[1]),
    .a(lcd_controller_1__7_segment_1[2]), .b(lcd_controller_1__7_segment_1[3]),
    .e(lcd_controller_1__7_segment_1[4]), .d(lcd_controller_1__7_segment_1[5]),
    .c(lcd_controller_1__7_segment_1[6]));  // open: dp
  Button _9 (.out(_9_out));
  Button _6 (.out(_6_out));
  Button _3 (.out(_3_out));
  Button button (.out(button_out));
  _7_Segment_Display u_7_segment_display_11 (
    .g(lcd_controller_1__7_segment_0[0]), .f(lcd_controller_1__7_segment_0[1]),
    .a(lcd_controller_1__7_segment_0[2]), .b(lcd_controller_1__7_segment_0[3]),
    .e(lcd_controller_1__7_segment_0[4]), .d(lcd_controller_1__7_segment_0[5]),
    .c(lcd_controller_1__7_segment_0[6]));  // open: dp
  Button button_2 (.out(button_2_out));
  Button button_3 (.out(button_3_out));
  Button button_4 (.out(button_4_out));
  Button button_5 (.out(button_5_out));

  // Notes on the sheet:
  //   From $t8
  //   From $t9
  //   Write Data to $t9
  //   Write Signal for $t9
endmodule

module LCD_Controller (
  input  [31:0] From__t8,
  output [6:0] Minus,
  output [6:0] _7_Segment_9,
  output [6:0] _7_Segment_8,
  output [6:0] _7_Segment_7,
  output [6:0] _7_Segment_6,
  output [6:0] _7_Segment_5,
  output [6:0] _7_Segment_4,
  output [6:0] _7_Segment_3,
  output [6:0] _7_Segment_2,
  output [6:0] _7_Segment_1,
  output [6:0] _7_Segment_0
);

  wire [3:0] binarytobcd_1_bcd0, binarytobcd_1_bcd1, binarytobcd_1_bcd2, binarytobcd_1_bcd3,
       binarytobcd_1_bcd4, binarytobcd_1_bcd5, binarytobcd_1_bcd6, binarytobcd_1_bcd7, binarytobcd_1_bcd8,
       binarytobcd_1_bcd9;

  BinaryToBCD binarytobcd_1 (
    .Input(From__t8), .Minus(Minus[0]), .BCD9(binarytobcd_1_bcd9), .BCD8(binarytobcd_1_bcd8),
    .BCD7(binarytobcd_1_bcd7), .BCD6(binarytobcd_1_bcd6), .BCD5(binarytobcd_1_bcd5),
    .BCD4(binarytobcd_1_bcd4), .BCD3(binarytobcd_1_bcd3), .BCD2(binarytobcd_1_bcd2),
    .BCD1(binarytobcd_1_bcd1), .BCD0(binarytobcd_1_bcd0));
  _7_Segment_Controller u_7_segment_controller_1 (.BCD(binarytobcd_1_bcd9), .out_2(_7_Segment_9));
  _7_Segment_Controller u_7_segment_controller_2 (.BCD(binarytobcd_1_bcd8), .out_2(_7_Segment_8));
  _7_Segment_Controller u_7_segment_controller_3 (.BCD(binarytobcd_1_bcd7), .out_2(_7_Segment_7));
  _7_Segment_Controller u_7_segment_controller_4 (.BCD(binarytobcd_1_bcd6), .out_2(_7_Segment_6));
  _7_Segment_Controller u_7_segment_controller_5 (.BCD(binarytobcd_1_bcd5), .out_2(_7_Segment_5));
  _7_Segment_Controller u_7_segment_controller_6 (.BCD(binarytobcd_1_bcd4), .out_2(_7_Segment_4));
  _7_Segment_Controller u_7_segment_controller_7 (.BCD(binarytobcd_1_bcd3), .out_2(_7_Segment_3));
  _7_Segment_Controller u_7_segment_controller_8 (.BCD(binarytobcd_1_bcd2), .out_2(_7_Segment_2));
  _7_Segment_Controller u_7_segment_controller_9 (.BCD(binarytobcd_1_bcd1), .out_2(_7_Segment_1));
  _7_Segment_Controller u_7_segment_controller_10 (.BCD(binarytobcd_1_bcd0), .out_2(_7_Segment_0));

  assign Minus[6:1] = {6{1'b0}};
endmodule

module _7_Segment_Controller (
  input  [3:0] BCD,
  output [6:0] out_2
);

  wire and_1_out, and_2_out, and_3_out, and_4_out, and_5_out, and_6_out, and_7_out, and_8_out, and_9_out,
       and_10_out, and_11_out, and_12_out, and_13_out, and_14_out, and_15_out, and_16_out, not_1_out,
       not_2_out, not_3_out, not_4_out, not_5_out, not_6_out, not_7_out, not_8_out, not_9_out, not_10_out,
       not_11_out, not_12_out, not_13_out, not_14_out, not_15_out, not_16_out, not_17_out, not_18_out,
       not_19_out, not_20_out, not_21_out;

  not not_1 (not_1_out, BCD[2]);
  not not_2 (not_2_out, BCD[0]);
  not not_3 (not_3_out, BCD[1]);
  not not_4 (not_4_out, BCD[1]);
  not not_5 (not_5_out, BCD[0]);
  not not_6 (not_6_out, BCD[1]);
  not not_7 (not_7_out, BCD[0]);
  not not_8 (not_8_out, BCD[2]);
  not not_9 (not_9_out, BCD[0]);
  not not_10 (not_10_out, BCD[1]);
  not not_11 (not_11_out, BCD[0]);
  not not_12 (not_12_out, BCD[2]);
  not not_13 (not_13_out, BCD[0]);
  not not_14 (not_14_out, BCD[0]);
  not not_15 (not_15_out, BCD[2]);
  not not_16 (not_16_out, BCD[0]);
  not not_17 (not_17_out, BCD[2]);
  not not_18 (not_18_out, BCD[0]);
  not not_19 (not_19_out, BCD[1]);
  not not_20 (not_20_out, BCD[1]);
  and and_1 (and_1_out, not_1_out, BCD[1]);
  and and_2 (and_2_out, BCD[1], not_2_out);
  and and_3 (and_3_out, BCD[2], not_3_out);
  and and_4 (and_4_out, not_4_out, not_5_out);
  and and_5 (and_5_out, BCD[2], not_6_out);
  and and_6 (and_6_out, BCD[2], not_7_out);
  and and_7 (and_7_out, not_8_out, not_9_out);
  and and_8 (and_8_out, BCD[2], BCD[0]);
  not not_21 (not_21_out, BCD[2]);
  and and_9 (and_9_out, not_10_out, not_11_out);
  and and_10 (and_10_out, BCD[1], BCD[0]);
  and and_11 (and_11_out, not_12_out, not_13_out);
  and and_12 (and_12_out, BCD[1], not_14_out);
  and and_13 (and_13_out, not_15_out, not_16_out);
  and and_14 (and_14_out, not_17_out, BCD[1]);
  and and_15 (and_15_out, BCD[1], not_18_out);
  and and_16 (and_16_out, BCD[2], not_19_out, BCD[0]);
  or or_1 (out_2[6], not_20_out, BCD[0], BCD[2]);
  or or_2 (out_2[0], and_1_out, and_2_out, and_3_out, BCD[3]);
  or or_3 (out_2[1], and_4_out, and_5_out, and_6_out, BCD[3]);
  or or_4 (out_2[2], and_7_out, BCD[1], and_8_out, BCD[3]);
  or or_5 (out_2[3], not_21_out, and_9_out, and_10_out);
  or or_6 (out_2[4], and_11_out, and_12_out);
  or or_7 (out_2[5], and_13_out, and_14_out, and_15_out, and_16_out);
endmodule

module BinaryToBCD (
  input  [31:0] Input,
  output Minus,
  output [3:0] BCD9,
  output [3:0] BCD8,
  output [3:0] BCD7,
  output [3:0] BCD6,
  output [3:0] BCD5,
  output [3:0] BCD4,
  output [3:0] BCD3,
  output [3:0] BCD2,
  output [3:0] BCD1,
  output [3:0] BCD0
);

  wire [27:0] subtractor_1_out, subtractor_2_out, subtractor_3_out, subtractor_4_out, subtractor_5_out,
       subtractor_6_out, subtractor_7_out, subtractor_8_out, subtractor_9_out;
  wire [31:0] adder_1_out, divider_1_out, divider_2_out, divider_3_out, divider_4_out, divider_5_out,
       divider_6_out, divider_7_out, divider_8_out, multiplexer_1_out, multiplier_1_out, multiplier_2_out,
       multiplier_3_out, multiplier_4_out, multiplier_5_out, multiplier_6_out, multiplier_7_out,
       multiplier_8_out, multiplier_9_out, not_1_out;
  wire [31:4] divider_9_out;

  assign not_1_out = ~Input;  // NOT_Gate not_1, 32 bits wide
  Adder #(.width(32)) adder_1 (.a(not_1_out), .b(32'h1), .out(adder_1_out));  // open: cin, cout
  Multiplexer #(.width(32)) multiplexer_1 (
    .in0(Input), .in1(adder_1_out), .out(multiplexer_1_out), .sel(Input[31]));  // open: en
  Subtractor #(.width(32)) subtractor_1 (
    .a(multiplexer_1_out), .b(multiplier_1_out), .out({subtractor_1_out, BCD0}));  // open: bin, bout
  Multiplier #(.width(32)) multiplier_1 (.a(divider_1_out), .b(32'ha), .out(multiplier_1_out));  // open: cin, cout
  Divider #(.width(32)) divider_1 (.a(multiplexer_1_out), .b(32'ha), .out(divider_1_out));  // open: upper, rem
  Subtractor #(.width(32)) subtractor_2 (
    .a(divider_1_out), .b(multiplier_2_out), .out({subtractor_2_out, BCD1}));  // open: bin, bout
  Multiplier #(.width(32)) multiplier_2 (.a(divider_2_out), .b(32'ha), .out(multiplier_2_out));  // open: cin, cout
  Divider #(.width(32)) divider_2 (.a(divider_1_out), .b(32'ha), .out(divider_2_out));  // open: upper, rem
  Subtractor #(.width(32)) subtractor_3 (
    .a(divider_2_out), .b(multiplier_3_out), .out({subtractor_3_out, BCD2}));  // open: bin, bout
  Multiplier #(.width(32)) multiplier_3 (.a(divider_3_out), .b(32'ha), .out(multiplier_3_out));  // open: cin, cout
  Divider #(.width(32)) divider_3 (.a(divider_2_out), .b(32'ha), .out(divider_3_out));  // open: upper, rem
  Subtractor #(.width(32)) subtractor_4 (
    .a(divider_3_out), .b(multiplier_4_out), .out({subtractor_4_out, BCD3}));  // open: bin, bout
  Multiplier #(.width(32)) multiplier_4 (.a(divider_4_out), .b(32'ha), .out(multiplier_4_out));  // open: cin, cout
  Divider #(.width(32)) divider_4 (.a(divider_3_out), .b(32'ha), .out(divider_4_out));  // open: upper, rem
  Subtractor #(.width(32)) subtractor_5 (
    .a(divider_4_out), .b(multiplier_5_out), .out({subtractor_5_out, BCD4}));  // open: bin, bout
  Multiplier #(.width(32)) multiplier_5 (.a(divider_5_out), .b(32'ha), .out(multiplier_5_out));  // open: cin, cout
  Divider #(.width(32)) divider_5 (.a(divider_4_out), .b(32'ha), .out(divider_5_out));  // open: upper, rem
  Subtractor #(.width(32)) subtractor_6 (
    .a(divider_5_out), .b(multiplier_6_out), .out({subtractor_6_out, BCD5}));  // open: bin, bout
  Multiplier #(.width(32)) multiplier_6 (.a(divider_6_out), .b(32'ha), .out(multiplier_6_out));  // open: cin, cout
  Divider #(.width(32)) divider_6 (.a(divider_5_out), .b(32'ha), .out(divider_6_out));  // open: upper, rem
  Subtractor #(.width(32)) subtractor_7 (
    .a(divider_6_out), .b(multiplier_7_out), .out({subtractor_7_out, BCD6}));  // open: bin, bout
  Multiplier #(.width(32)) multiplier_7 (.a(divider_7_out), .b(32'ha), .out(multiplier_7_out));  // open: cin, cout
  Divider #(.width(32)) divider_7 (.a(divider_6_out), .b(32'ha), .out(divider_7_out));  // open: upper, rem
  Subtractor #(.width(32)) subtractor_8 (
    .a(divider_7_out), .b(multiplier_8_out), .out({subtractor_8_out, BCD7}));  // open: bin, bout
  Multiplier #(.width(32)) multiplier_8 (.a(divider_8_out), .b(32'ha), .out(multiplier_8_out));  // open: cin, cout
  Divider #(.width(32)) divider_8 (.a(divider_7_out), .b(32'ha), .out(divider_8_out));  // open: upper, rem
  Subtractor #(.width(32)) subtractor_9 (
    .a(divider_8_out), .b(multiplier_9_out), .out({subtractor_9_out, BCD8}));  // open: bin, bout
  Multiplier #(.width(32)) multiplier_9 (
    .a({divider_9_out, BCD9}), .b(32'ha), .out(multiplier_9_out));  // open: cin, cout
  Divider #(.width(32)) divider_9 (.a(divider_8_out), .b(32'ha), .out({divider_9_out, BCD9}));  // open: upper, rem

  assign Minus = Input[31];
endmodule

module Keypad_Controller (
  input  C,
  input  in_2,
  input  in_3,
  input  in_4,
  input  in_5,
  input  in_6,
  input  _9,
  input  _8,
  input  _7,
  input  _6,
  input  _5,
  input  _4,
  input  _3,
  input  _2,
  input  _1,
  input  _0,
  input  [31:0] From__t9,
  output Write,
  output [31:0] Output
);

  wire iszero_1_out_2, iszero_2_out_2;
  wire [3:0] or_4_out;
  wire [15:0] and_1_out;

  and and_1 (and_1_out[0], C, iszero_1_out_2);
  and and_2 (and_1_out[1], in_2, iszero_1_out_2);
  and and_3 (and_1_out[2], in_3, iszero_1_out_2);
  and and_4 (and_1_out[3], in_4, iszero_1_out_2);
  and and_5 (and_1_out[4], in_5, iszero_1_out_2);
  and and_6 (and_1_out[5], in_6, iszero_1_out_2);
  and and_7 (and_1_out[6], _9, iszero_1_out_2);
  and and_8 (and_1_out[7], _8, iszero_1_out_2);
  and and_9 (and_1_out[8], _7, iszero_1_out_2);
  and and_10 (and_1_out[9], _6, iszero_1_out_2);
  and and_11 (and_1_out[10], _5, iszero_1_out_2);
  and and_12 (and_1_out[11], _4, iszero_1_out_2);
  and and_13 (and_1_out[12], _3, iszero_1_out_2);
  and and_14 (and_1_out[13], _2, iszero_1_out_2);
  and and_15 (and_1_out[14], _1, iszero_1_out_2);
  and and_16 (and_1_out[15], _0, iszero_1_out_2);
  isZero iszero_1 (.Input(From__t9), .out_2(iszero_1_out_2));
  or or_1 (or_4_out[3], and_1_out[0], and_1_out[1], and_1_out[2], and_1_out[3], and_1_out[4], and_1_out[5], and_1_out[6], and_1_out[7]);
  or or_2 (or_4_out[2], and_1_out[8], and_1_out[9], and_1_out[10], and_1_out[11], and_1_out[0], and_1_out[1], and_1_out[2], and_1_out[3]);
  or or_3 (or_4_out[1], and_1_out[12], and_1_out[13], and_1_out[9], and_1_out[8], and_1_out[5], and_1_out[4], and_1_out[1], and_1_out[0]);
  or or_4 (or_4_out[0], and_1_out[12], and_1_out[14], and_1_out[10], and_1_out[8], and_1_out[6], and_1_out[4], and_1_out[2], and_1_out[0]);
  isZero iszero_2 (.Input({{16{1'b0}}, and_1_out}), .out_2(iszero_2_out_2));
  not not_1 (Write, iszero_2_out_2);
  assign Output = Write ? {28'h8000000, or_4_out} : 32'bz;  // Controlled_Buffer controlled_buffer_1
endmodule

module isZero (
  input  [31:0] Input,
  output out_2
);

  wire or_1_out;

  or or_1 (or_1_out, Input[0], Input[1], Input[2], Input[3], Input[4], Input[5], Input[6], Input[7], Input[8], Input[9], Input[10], Input[11], Input[12], Input[13], Input[14], Input[15], Input[16], Input[17], Input[18], Input[19], Input[20], Input[21], Input[22], Input[23], Input[24], Input[25], Input[26], Input[27], Input[28], Input[29], Input[30], Input[31]);
  not not_1 (out_2, or_1_out);
endmodule

// MEM
module Instruction_Memory__TO_DO (
  input  [15:0] PC,
  output [31:0] Output
);

  ROM #(.addrWidth(16), .dataWidth(32)) rom_1 (.addr(PC), .data(Output));  // open: sel

  // Notes on the sheet:
  //   contents of rom_1 (hex, n*v repeats v):
  //   4020 4820 5020 5820 6020 6820 7020 8020 8820 9020 2013000a a020 a820 c820 c020 1320ffff 19c840
  //   19c842 195020 294b000a 20010000 102b0026 20010000 102d0002 20010000 102e0011 20010000 14280004
  //   194020 c820 8c020 810000f 8a820 22940001 1154020 22940001 1693fffd a020 a820 1194020 c820 8c020
  //   810000f 20010000 14290004 194820 c820 9c020 810000f 9a820 22940001 1354820 22940001 1693fffd a020
  //   a820 1394820 c820 9c020 810000f c820 2001000e 102a0021 2001000f 102affbf 200d0001 a8020 810000f
  //   1099020 12c020 810006a 1099022 12c020 810006a 12290006 2489020 22310001 1629fffc 8820 12c020 810006a
  //   99020 12c020 810006a 12280008 1094022 22520001 290c0001 20010001 102c0001 8100055 12c020 810006a
  //   89020 12c020 810006a c820 200e0001 2001000a 1030ffe0 2001000b 1030ffe1 2001000c 1030ffe2 2001000d
  //   1030ffea c820 8820 7020 124020 9020 4820 810000f
endmodule

module Shift_Left__TO_DO (
  input  [31:0] Input,
  input  [4:0] Shamt,
  output [31:0] Output
);

  Shifter #(.width(32)) shifter_1 (.in(Input), .\dist (Shamt), .out(Output));
endmodule

module Shift_Right__TO_DO (
  input  [31:0] Input,
  input  [4:0] shamt,
  output [31:0] \output 
);

  Shifter #(.width(32), .shift("lr")) shifter_1 (.in(Input), .\dist (shamt), .out(\output ));
endmodule

module Sign_Extend__TO_DO (
  input  [15:0] Input,
  output [31:0] Output
);


  assign Output = {{17{Input[15]}}, Input[14:0]};
endmodule

module _32_bit_ALU__TO_DO (
  input  [31:0] A,
  input  [31:0] B,
  input  [3:0] Operation,
  output [31:0] Result,
  output Zero
);

  wire or_2_out;
  wire [31:0] adder_1_out, and_1_out, multiplexer_1_out, multiplexer_2_out, not_1_out, not_2_out, or_1_out,
       sign_extend_3_the_revenge_1_out_2;

  assign not_1_out = ~A;  // NOT_Gate not_1, 32 bits wide
  assign not_2_out = ~B;  // NOT_Gate not_2, 32 bits wide
  Multiplexer #(.width(32)) multiplexer_1 (
    .in0(A), .in1(not_1_out), .out(multiplexer_1_out), .sel(Operation[3]));  // open: en
  Multiplexer #(.width(32)) multiplexer_2 (
    .in0(B), .in1(not_2_out), .out(multiplexer_2_out), .sel(Operation[2]));  // open: en
  assign and_1_out = multiplexer_1_out & multiplexer_2_out;  // AND_Gate and_1, 32 bits wide
  assign or_1_out = multiplexer_1_out | multiplexer_2_out;  // OR_Gate or_1, 32 bits wide
  Adder #(.width(32)) adder_1 (
    .a(multiplexer_1_out), .b(multiplexer_2_out), .out(adder_1_out), .cin(Operation[2]));  // open: cout
  Sign_Extend_3__The_Revenge sign_extend_3_the_revenge_1 (
    .Input(adder_1_out[31]), .out_2(sign_extend_3_the_revenge_1_out_2));
  Multiplexer #(.select(2), .width(32)) multiplexer_3 (
    .in0(and_1_out), .in1(or_1_out), .in2(adder_1_out), .in3(sign_extend_3_the_revenge_1_out_2),
    .out(Result), .sel(Operation[1:0]));  // open: en
  or or_2 (or_2_out, Result[0], Result[1], Result[2], Result[3], Result[4], Result[5], Result[6], Result[7], Result[8], Result[9], Result[10], Result[11], Result[12], Result[13], Result[14], Result[15], Result[17], Result[18], Result[19], Result[20], Result[21], Result[22], Result[23], Result[24], Result[25], Result[26], Result[27], Result[28], Result[29], Result[30], Result[31]);
  not not_3 (Zero, or_2_out);
endmodule

// Reg
module Register_File__TO_DO (
  input  [4:0] Read_Register_1,
  input  [4:0] Read_Register_2,
  input  [31:0] Write_Data,
  input  RegWrite,
  input  [4:0] Write_Register,
  input  [31:0] Write_from_Keypad,
  input  Write_signal,
  input  Clock,
  output [31:0] Read_Data_1,
  output [31:0] Read_Data_2,
  output [31:0] ToLCD,
  output [31:0] To_KeyPad
);

  wire controlled_buffer_2_out, demultiplexer_2_out0, demultiplexer_2_out1, demultiplexer_2_out2,
       demultiplexer_2_out3, demultiplexer_2_out4, demultiplexer_2_out5, demultiplexer_2_out6,
       demultiplexer_2_out7, demultiplexer_2_out8, demultiplexer_2_out9, demultiplexer_2_out10,
       demultiplexer_2_out11, demultiplexer_2_out12, demultiplexer_2_out13, demultiplexer_2_out14,
       demultiplexer_2_out15, demultiplexer_2_out16, demultiplexer_2_out17, demultiplexer_2_out18,
       demultiplexer_2_out19, demultiplexer_2_out20, demultiplexer_2_out21, demultiplexer_2_out22,
       demultiplexer_2_out23, demultiplexer_2_out24, demultiplexer_2_out25, demultiplexer_2_out26,
       demultiplexer_2_out27, demultiplexer_2_out28, demultiplexer_2_out29, demultiplexer_2_out30,
       demultiplexer_2_out31;
  wire [31:0] controlled_buffer_1_out, demultiplexer_1_out0, demultiplexer_1_out1, demultiplexer_1_out2,
       demultiplexer_1_out3, demultiplexer_1_out4, demultiplexer_1_out5, demultiplexer_1_out6,
       demultiplexer_1_out7, demultiplexer_1_out8, demultiplexer_1_out9, demultiplexer_1_out10,
       demultiplexer_1_out11, demultiplexer_1_out12, demultiplexer_1_out13, demultiplexer_1_out14,
       demultiplexer_1_out15, demultiplexer_1_out16, demultiplexer_1_out17, demultiplexer_1_out18,
       demultiplexer_1_out19, demultiplexer_1_out20, demultiplexer_1_out21, demultiplexer_1_out22,
       demultiplexer_1_out23, demultiplexer_1_out24, demultiplexer_1_out25, demultiplexer_1_out26,
       demultiplexer_1_out27, demultiplexer_1_out28, demultiplexer_1_out29, demultiplexer_1_out30,
       demultiplexer_1_out31, REG0_q, REG1_q, REG2_q, REG3_q, REG4_q, REG5_q, REG6_q, REG7_q, REG8_q, REG9_q,
       REG10_q, REg11_q, REG12_q, REG13_q, REG14_q, REG15_q, REG16_q, REG17_q, REG18_q, REG19_q, REG20_q,
       REG21_q, REG22_q, REG23_q, REG26_q, REG27_q, REG28_q, REG29_q, REG30_q, REG31_q;

  Demultiplexer #(.select(5), .width(32)) demultiplexer_1 (
    .out0(demultiplexer_1_out0), .out1(demultiplexer_1_out1), .out2(demultiplexer_1_out2),
    .out3(demultiplexer_1_out3), .out4(demultiplexer_1_out4), .out5(demultiplexer_1_out5),
    .out6(demultiplexer_1_out6), .out7(demultiplexer_1_out7), .out8(demultiplexer_1_out8),
    .out9(demultiplexer_1_out9), .out10(demultiplexer_1_out10), .out11(demultiplexer_1_out11),
    .out12(demultiplexer_1_out12), .out13(demultiplexer_1_out13), .out14(demultiplexer_1_out14),
    .out15(demultiplexer_1_out15), .out16(demultiplexer_1_out16), .out17(demultiplexer_1_out17),
    .out18(demultiplexer_1_out18), .out19(demultiplexer_1_out19), .out20(demultiplexer_1_out20),
    .out21(demultiplexer_1_out21), .out22(demultiplexer_1_out22), .out23(demultiplexer_1_out23),
    .out24(demultiplexer_1_out24), .out25(demultiplexer_1_out25), .out26(demultiplexer_1_out26),
    .out27(demultiplexer_1_out27), .out28(demultiplexer_1_out28), .out29(demultiplexer_1_out29),
    .out30(demultiplexer_1_out30), .out31(demultiplexer_1_out31), .in(Write_Data), .sel(Write_Register),
    .en(RegWrite));
  Demultiplexer #(.select(5)) demultiplexer_2 (
    .out0(demultiplexer_2_out0), .out1(demultiplexer_2_out1), .out2(demultiplexer_2_out2),
    .out3(demultiplexer_2_out3), .out4(demultiplexer_2_out4), .out5(demultiplexer_2_out5),
    .out6(demultiplexer_2_out6), .out7(demultiplexer_2_out7), .out8(demultiplexer_2_out8),
    .out9(demultiplexer_2_out9), .out10(demultiplexer_2_out10), .out11(demultiplexer_2_out11),
    .out12(demultiplexer_2_out12), .out13(demultiplexer_2_out13), .out14(demultiplexer_2_out14),
    .out15(demultiplexer_2_out15), .out16(demultiplexer_2_out16), .out17(demultiplexer_2_out17),
    .out18(demultiplexer_2_out18), .out19(demultiplexer_2_out19), .out20(demultiplexer_2_out20),
    .out21(demultiplexer_2_out21), .out22(demultiplexer_2_out22), .out23(demultiplexer_2_out23),
    .out24(demultiplexer_2_out24), .out25(demultiplexer_2_out25), .out26(demultiplexer_2_out26),
    .out27(demultiplexer_2_out27), .out28(demultiplexer_2_out28), .out29(demultiplexer_2_out29),
    .out30(demultiplexer_2_out30), .out31(demultiplexer_2_out31), .in(RegWrite), .sel(Write_Register));  // open: en
  assign controlled_buffer_1_out = Write_signal ? Write_from_Keypad : 32'bz;  // Controlled_Buffer controlled_buffer_1
  assign controlled_buffer_2_out = Write_signal ? Write_signal : 1'bz;  // Controlled_Buffer controlled_buffer_2
  assign controlled_buffer_1_out = demultiplexer_2_out25 ? demultiplexer_1_out25 : 32'bz;  // Controlled_Buffer controlled_buffer_3
  assign controlled_buffer_2_out = demultiplexer_2_out25 ? demultiplexer_2_out25 : 1'bz;  // Controlled_Buffer controlled_buffer_4
  Register #(.width(32)) REG0 (
    .D(demultiplexer_1_out0), .en(demultiplexer_2_out0), .Q(REG0_q), .clk(Clock));  // open: clr
  Register #(.width(32)) REG1 (
    .D(demultiplexer_1_out1), .en(demultiplexer_2_out1), .Q(REG1_q), .clk(Clock));  // open: clr
  Register #(.width(32)) REG2 (
    .D(demultiplexer_1_out2), .en(demultiplexer_2_out2), .Q(REG2_q), .clk(Clock));  // open: clr
  Register #(.width(32)) REG3 (
    .D(demultiplexer_1_out3), .en(demultiplexer_2_out3), .Q(REG3_q), .clk(Clock));  // open: clr
  Register #(.width(32)) REG4 (
    .D(demultiplexer_1_out4), .en(demultiplexer_2_out4), .Q(REG4_q), .clk(Clock));  // open: clr
  Register #(.width(32)) REG5 (
    .D(demultiplexer_1_out5), .en(demultiplexer_2_out5), .Q(REG5_q), .clk(Clock));  // open: clr
  Register #(.width(32)) REG6 (
    .D(demultiplexer_1_out6), .en(demultiplexer_2_out6), .Q(REG6_q), .clk(Clock));  // open: clr
  Register #(.width(32)) REG7 (
    .D(demultiplexer_1_out7), .en(demultiplexer_2_out7), .Q(REG7_q), .clk(Clock));  // open: clr
  Register #(.width(32)) REG8 (
    .D(demultiplexer_1_out8), .en(demultiplexer_2_out8), .Q(REG8_q), .clk(Clock));  // open: clr
  Register #(.width(32)) REG9 (
    .D(demultiplexer_1_out9), .en(demultiplexer_2_out9), .Q(REG9_q), .clk(Clock));  // open: clr
  Register #(.width(32)) REG10 (
    .D(demultiplexer_1_out10), .en(demultiplexer_2_out10), .Q(REG10_q), .clk(Clock));  // open: clr
  Register #(.width(32)) REg11 (
    .D(demultiplexer_1_out11), .en(demultiplexer_2_out11), .Q(REg11_q), .clk(Clock));  // open: clr
  Register #(.width(32)) REG12 (
    .D(demultiplexer_1_out12), .en(demultiplexer_2_out12), .Q(REG12_q), .clk(Clock));  // open: clr
  Register #(.width(32)) REG13 (
    .D(demultiplexer_1_out13), .en(demultiplexer_2_out13), .Q(REG13_q), .clk(Clock));  // open: clr
  Register #(.width(32)) REG14 (
    .D(demultiplexer_1_out14), .en(demultiplexer_2_out14), .Q(REG14_q), .clk(Clock));  // open: clr
  Register #(.width(32)) REG15 (
    .D(demultiplexer_1_out15), .en(demultiplexer_2_out15), .Q(REG15_q), .clk(Clock));  // open: clr
  Register #(.width(32)) REG16 (
    .D(demultiplexer_1_out16), .en(demultiplexer_2_out16), .Q(REG16_q), .clk(Clock));  // open: clr
  Register #(.width(32)) REG17 (
    .D(demultiplexer_1_out17), .en(demultiplexer_2_out17), .Q(REG17_q), .clk(Clock));  // open: clr
  Register #(.width(32)) REG18 (
    .D(demultiplexer_1_out18), .en(demultiplexer_2_out18), .Q(REG18_q), .clk(Clock));  // open: clr
  Register #(.width(32)) REG19 (
    .D(demultiplexer_1_out19), .en(demultiplexer_2_out19), .Q(REG19_q), .clk(Clock));  // open: clr
  Register #(.width(32)) REG20 (
    .D(demultiplexer_1_out20), .en(demultiplexer_2_out20), .Q(REG20_q), .clk(Clock));  // open: clr
  Register #(.width(32)) REG21 (
    .D(demultiplexer_1_out21), .en(demultiplexer_2_out21), .Q(REG21_q), .clk(Clock));  // open: clr
  Register #(.width(32)) REG22 (
    .D(demultiplexer_1_out22), .en(demultiplexer_2_out22), .Q(REG22_q), .clk(Clock));  // open: clr
  Register #(.width(32)) REG23 (
    .D(demultiplexer_1_out23), .en(demultiplexer_2_out23), .Q(REG23_q), .clk(Clock));  // open: clr
  Register #(.width(32)) T8 (
    .D(demultiplexer_1_out24), .en(demultiplexer_2_out24), .Q(ToLCD), .clk(Clock));  // open: clr
  Register #(.width(32)) T9 (
    .D(controlled_buffer_1_out), .en(controlled_buffer_2_out), .Q(To_KeyPad), .clk(Clock));  // open: clr
  Register #(.width(32)) REG26 (
    .D(demultiplexer_1_out26), .en(demultiplexer_2_out26), .Q(REG26_q), .clk(Clock));  // open: clr
  Register #(.width(32)) REG27 (
    .D(demultiplexer_1_out27), .en(demultiplexer_2_out27), .Q(REG27_q), .clk(Clock));  // open: clr
  Register #(.width(32)) REG28 (
    .D(demultiplexer_1_out28), .en(demultiplexer_2_out28), .Q(REG28_q), .clk(Clock));  // open: clr
  Register #(.width(32)) REG29 (
    .D(demultiplexer_1_out29), .en(demultiplexer_2_out29), .Q(REG29_q), .clk(Clock));  // open: clr
  Register #(.width(32)) REG30 (
    .D(demultiplexer_1_out30), .en(demultiplexer_2_out30), .Q(REG30_q), .clk(Clock));  // open: clr
  Register #(.width(32)) REG31 (
    .D(demultiplexer_1_out31), .en(demultiplexer_2_out31), .Q(REG31_q), .clk(Clock));  // open: clr
  Multiplexer #(.select(5), .width(32)) multiplexer_1 (
    .in0(REG0_q), .in1(REG1_q), .in2(REG2_q), .in3(REG3_q), .in4(REG4_q), .in5(REG5_q), .in6(REG6_q),
    .in7(REG7_q), .in8(REG8_q), .in9(REG9_q), .in10(REG10_q), .in11(REg11_q), .in12(REG12_q), .in13(REG13_q),
    .in14(REG14_q), .in15(REG15_q), .in16(REG16_q), .in17(REG17_q), .in18(REG18_q), .in19(REG19_q),
    .in20(REG20_q), .in21(REG21_q), .in22(REG22_q), .in23(REG23_q), .in24(ToLCD), .in25(To_KeyPad),
    .in26(REG26_q), .in27(REG27_q), .in28(REG28_q), .in29(REG29_q), .in30(REG30_q), .in31(REG31_q),
    .out(Read_Data_1), .sel(Read_Register_1));  // open: en
  Multiplexer #(.select(5), .width(32)) multiplexer_2 (
    .in0(REG0_q), .in1(REG1_q), .in2(REG2_q), .in3(REG3_q), .in4(REG4_q), .in5(REG5_q), .in6(REG6_q),
    .in7(REG7_q), .in8(REG8_q), .in9(REG9_q), .in10(REG10_q), .in11(REg11_q), .in12(REG12_q), .in13(REG13_q),
    .in14(REG14_q), .in15(REG15_q), .in16(REG16_q), .in17(REG17_q), .in18(REG18_q), .in19(REG19_q),
    .in20(REG20_q), .in21(REG21_q), .in22(REG22_q), .in23(REG23_q), .in24(ToLCD), .in25(To_KeyPad),
    .in26(REG26_q), .in27(REG27_q), .in28(REG28_q), .in29(REG29_q), .in30(REG30_q), .in31(REG31_q),
    .out(Read_Data_2), .sel(Read_Register_2));  // open: en
endmodule

// CU
module Control_Unit__TO_DO (
  input  [5:0] Input,
  output RegWrite,
  output RegDst,
  output Jump,
  output branch,
  output Branch_Not_Equal,
  output ALU_Src,
  output [1:0] ALU_OP
);

  wire not_1_out, not_3_out, not_4_out, not_5_out, not_6_out, not_7_out, not_8_out, or_1_out;

  not not_1 (not_1_out, Input[3]);
  not not_2 (RegDst, Input[3]);
  not not_3 (not_3_out, Input[5]);
  not not_4 (not_4_out, Input[4]);
  not not_5 (not_5_out, Input[3]);
  not not_6 (not_6_out, Input[2]);
  not not_7 (not_7_out, Input[0]);
  ALU_OP alu_op_1 (.OP(Input), .RegWrite(RegWrite), .ALU_OP(ALU_OP));
  or or_1 (or_1_out, Input[0], Input[1], Input[2]);
  and and_1 (Jump, not_3_out, not_4_out, not_5_out, not_6_out, Input[1], not_7_out);
  and and_2 (branch, Input[2], not_1_out);
  not not_8 (not_8_out, or_1_out);
  or or_2 (RegWrite, not_8_out, Input[3]);
  and and_3 (Branch_Not_Equal, branch, Input[0]);

  assign ALU_Src = Input[3];
endmodule

// SL2
module Shift_Left_2 (
  input  [31:0] Input,
  output [31:0] Output
);

  Multiplier #(.width(32)) multiplier_1 (.a(Input), .b(32'h4), .out(Output));  // open: cin, cout
endmodule

module baseC (
  input  [31:0] Write_From_Keypad,
  input  Write_Signal,
  output [31:0] ToLCD,
  output [31:0] ToKeypad
);

  wire alu_wrap_1_zero, and_1_out, clock_1_out, control_unit_to_do_1_alu_src, control_unit_to_do_1_branch,
       control_unit_to_do_1_branch_not_equal, control_unit_to_do_1_jump, control_unit_to_do_1_regdst,
       control_unit_to_do_1_regwrite, multiplexer_5_out, not_1_out;
  wire [1:0] control_unit_to_do_1_alu_op, shiftc_1_out_2;
  wire [3:0] adder_1_out, alu_control_1_alu_op_2;
  wire [4:0] multiplexer_1_out;
  wire [27:0] adder_1_out_2, shift_left2_the_sequel_1_uhh;
  wire [31:0] adder_2_out, alu_wrap_1_result, instruction_memory_to_do_1_output, multiplexer_2_out,
       multiplexer_3_out, multiplexer_4_out, PC_q, register_file_to_do_1_read_data_1,
       register_file_to_do_1_read_data_2, shift_left_2_1_output, Sign_Extend_output;

  Register #(.width(32)) PC (.D(multiplexer_4_out), .Q(PC_q), .clk(clock_1_out));  // open: en, clr
  Adder #(.width(32)) adder_1 (.a(PC_q), .b(32'h4), .out({adder_1_out, adder_1_out_2}));  // open: cin, cout
  Instruction_Memory__TO_DO instruction_memory_to_do_1 (.PC(PC_q[17:2]), .Output(instruction_memory_to_do_1_output));
  Shift_Left2__The_Sequel shift_left2_the_sequel_1 (
    .ohh_yeah(instruction_memory_to_do_1_output[25:0]), .Uhh(shift_left2_the_sequel_1_uhh));
  Control_Unit__TO_DO control_unit_to_do_1 (
    .Input(instruction_memory_to_do_1_output[31:26]), .RegWrite(control_unit_to_do_1_regwrite),
    .RegDst(control_unit_to_do_1_regdst), .Jump(control_unit_to_do_1_jump),
    .branch(control_unit_to_do_1_branch), .Branch_Not_Equal(control_unit_to_do_1_branch_not_equal),
    .ALU_Src(control_unit_to_do_1_alu_src), .ALU_OP(control_unit_to_do_1_alu_op));
  Multiplexer #(.width(5)) multiplexer_1 (
    .in0(instruction_memory_to_do_1_output[20:16]), .in1(instruction_memory_to_do_1_output[15:11]),
    .out(multiplexer_1_out), .sel(control_unit_to_do_1_regdst));  // open: en
  Shift_Left_2 shift_left_2_1 (.Input(Sign_Extend_output), .Output(shift_left_2_1_output));
  Clock clock_1 (.out(clock_1_out));
  Sign_Extend__TO_DO Sign_Extend (.Input(instruction_memory_to_do_1_output[15:0]), .Output(Sign_Extend_output));
  ALU_Control alu_control_1 (
    .\function (instruction_memory_to_do_1_output[5:0]), .ALU_OP(control_unit_to_do_1_alu_op),
    .OPCODE(instruction_memory_to_do_1_output[31:26]), .ALU_OP_2(alu_control_1_alu_op_2));
  Adder #(.width(32)) adder_2 (
    .a({adder_1_out, adder_1_out_2}), .b(shift_left_2_1_output), .out(adder_2_out));  // open: cin, cout
  Register_File__TO_DO register_file_to_do_1 (
    .Read_Register_1(instruction_memory_to_do_1_output[25:21]),
    .Read_Register_2(instruction_memory_to_do_1_output[20:16]), .Write_Data(alu_wrap_1_result),
    .Write_Register(multiplexer_1_out), .Write_from_Keypad(Write_From_Keypad), .Write_signal(Write_Signal),
    .RegWrite(control_unit_to_do_1_regwrite), .Clock(clock_1_out),
    .Read_Data_1(register_file_to_do_1_read_data_1), .Read_Data_2(register_file_to_do_1_read_data_2),
    .ToLCD(ToLCD), .To_KeyPad(ToKeypad));
  Multiplexer #(.width(32)) multiplexer_2 (
    .in0({adder_1_out, adder_1_out_2}), .in1(adder_2_out), .out(multiplexer_2_out), .sel(multiplexer_5_out));  // open: en
  Multiplexer #(.width(32)) multiplexer_3 (
    .in0(register_file_to_do_1_read_data_2), .in1(Sign_Extend_output), .out(multiplexer_3_out),
    .sel(control_unit_to_do_1_alu_src));  // open: en
  Multiplexer #(.width(32)) multiplexer_4 (
    .in0(multiplexer_2_out), .in1({adder_1_out, shift_left2_the_sequel_1_uhh}), .out(multiplexer_4_out),
    .sel(control_unit_to_do_1_jump));  // open: en
  and and_1 (and_1_out, control_unit_to_do_1_branch, alu_wrap_1_zero);
  ALU_Wrap alu_wrap_1 (
    .ALU_OP(alu_control_1_alu_op_2), .A(register_file_to_do_1_read_data_1), .B(multiplexer_3_out),
    .shamt(instruction_memory_to_do_1_output[10:6]), .Shift_operation(shiftc_1_out_2),
    .Zero(alu_wrap_1_zero), .Result(alu_wrap_1_result));
  ShiftC shiftc_1 (.Input(instruction_memory_to_do_1_output[5:0]), .out_2(shiftc_1_out_2));
  Multiplexer multiplexer_5 (
    .in0(and_1_out), .in1(not_1_out), .out(multiplexer_5_out), .sel(control_unit_to_do_1_branch_not_equal));  // open: en
  not not_1 (not_1_out, and_1_out);
endmodule

// ALU
module ALU_Wrap (
  input  [3:0] ALU_OP,
  input  [31:0] A,
  input  [31:0] B,
  input  [4:0] shamt,
  input  [1:0] Shift_operation,
  output Zero,
  output [31:0] Result
);

  wire [31:0] n32_bit_alu_to_do_1_result, shift_left_to_do_1_output, shift_right_to_do_1_output;

  _32_bit_ALU__TO_DO u_32_bit_alu_to_do_1 (
    .A(A), .B(B), .Operation(ALU_OP), .Result(n32_bit_alu_to_do_1_result), .Zero(Zero));
  Shift_Left__TO_DO shift_left_to_do_1 (.Input(B), .Shamt(shamt), .Output(shift_left_to_do_1_output));
  Shift_Right__TO_DO shift_right_to_do_1 (.Input(B), .shamt(shamt), .\output (shift_right_to_do_1_output));
  Multiplexer #(.select(2), .width(32)) multiplexer_1 (
    .in0(n32_bit_alu_to_do_1_result), .in2(shift_left_to_do_1_output), .in3(shift_right_to_do_1_output),
    .out(Result), .sel(Shift_operation));  // open: in1, en
endmodule

module ALU_Control (
  input  [5:0] \function ,
  input  [1:0] ALU_OP,
  input  [5:0] OPCODE,
  output [3:0] ALU_OP_2
);

  wire and_1_out, and_2_out, not_1_out;
  wire [2:0] or_1_out;
  wire [3:0] func_control_1_output;

  func_control func_control_1 (.Input(\function ), .\output (func_control_1_output));
  Multiplexer #(.select(2), .width(4)) multiplexer_1 (
    .in0(4'b0010), .in1(4'b0110), .in2(func_control_1_output), .in3({1'b0, or_1_out}), .out(ALU_OP_2),
    .sel(ALU_OP));  // open: en
  or or_1 (or_1_out[0], OPCODE[1], and_1_out);
  and and_1 (and_1_out, OPCODE[0], OPCODE[3]);
  not not_1 (not_1_out, OPCODE[3]);
  and and_2 (and_2_out, OPCODE[3], OPCODE[2]);
  not not_2 (or_1_out[1], and_2_out);
  or or_2 (or_1_out[2], OPCODE[1], not_1_out);
endmodule

module func_control (
  input  [5:0] Input,
  output [3:0] \output 
);

  not not_1 (\output [1], Input[2]);
  or or_1 (\output [0], Input[3], Input[0]);

  assign \output [3:2] = {1'b0, Input[1]};
endmodule

module ALU_OP (
  input  [5:0] OP,
  input  RegWrite,
  output [1:0] ALU_OP
);

  or or_1 (ALU_OP[0], OP[2], OP[3]);

  assign ALU_OP[1] = RegWrite;
endmodule

module ShiftC (
  input  [5:0] Input,
  output [1:0] out_2
);

  wire and_1_out, not_1_out, not_2_out, not_3_out, not_4_out, not_5_out, not_6_out;

  not not_1 (not_1_out, Input[0]);
  not not_2 (not_2_out, Input[1]);
  not not_3 (not_3_out, Input[2]);
  not not_4 (not_4_out, Input[3]);
  not not_5 (not_5_out, Input[4]);
  not not_6 (not_6_out, Input[5]);
  and and_1 (and_1_out, not_1_out, not_2_out, not_3_out, not_4_out, not_5_out, not_6_out);
  and and_2 (out_2[0], not_1_out, Input[1], not_3_out, not_4_out, not_5_out, not_6_out);
  or or_1 (out_2[1], and_1_out, out_2[0]);
endmodule

module Shift_Left2__The_Sequel (
  input  [25:0] ohh_yeah,
  output [27:0] Uhh
);


  assign Uhh = {ohh_yeah, 2'b00};
endmodule

module Sign_Extend_3__The_Revenge (
  input  Input,
  output [31:0] out_2
);


  assign out_2 = {{31{1'b0}}, Input};
endmodule
